# Fritzing sketch RRFTracker_multiplex (saved by Fritzing 0.9.2b)
breadboards: 1

parts:
  Composant3 = node32s
  Composant4 = Adafruit TCA9548A
  OLED_I2C2 = OLED 128x64 I2C Monochrome Display  # not connected
  OLED_I2C3 = OLED 128x64 I2C Monochrome Display  # not connected
  OLED_I2C4 = OLED 128x64 I2C Monochrome Display
  OLED_I2C5 = OLED 128x64 I2C Monochrome Display  # not connected
  R1 = Resistor [tolerance=±5% resistance=330 package=THT]
  R2 = Resistor [tolerance=±5% resistance=330 package=THT]
  R3 = Resistor [tolerance=±5% resistance=330 package=THT]
  LED1 = smd LED [color="Green (555nm)" package="1206 [SMD]"]
  LED2 = smd LED [color="Blue (430nm)" package="1206 [SMD]"]
  R4 = Resistor [tolerance=±5% resistance=330 package=THT]
  R5 = Resistor [tolerance=±5% resistance=330 package=THT]
  R6 = Resistor [tolerance=±5% resistance=330 package=THT]
  LED3 = smd LED [color="Green (555nm)" package="1206 [SMD]"]
  LED4 = smd LED [color="Green (555nm)" package="1206 [SMD]"]
  LED5 = smd LED [color="Green (555nm)" package="1206 [SMD]"]
  LED6 = smd LED [color="Red (633nm)" package="1206 [SMD]"]

nets:
  N1: Composant3.GND, R1.Pin_1, R2.Pin_1, R3.Pin_1, R4.Pin_1, R5.Pin_1, R6.Pin_1
  N2: Composant3.IO5, LED6.anode
  N3: Composant3.IO17, LED5.anode
  N4: Composant3.IO16, LED4.anode
  N5: Composant3.IO4, LED3.anode
  N6: Composant3.IO0, LED2.anode
  N7: Composant3.IO2, LED1.anode
  N8: Composant4.0SDA, OLED_I2C4.SDA
  N9: Composant4.0SCL, OLED_I2C4.SCK
  N10: R1.Pin_0, LED1.cathode
  N11: R2.Pin_0, LED2.cathode
  N12: R3.Pin_0, LED3.cathode
  N13: R4.Pin_0, LED4.cathode
  N14: R5.Pin_0, LED5.cathode
  N15: R6.Pin_0, LED6.cathode

custom parts:
  Adafruit TCA9548A: You just found the perfect I2C sensor, and you want to wire up two or three or more of them to your Arduino when you realize "Uh oh, this chip has a fixed I2C address, and from what I know about I2C, you cannot have two devices with the same address on the same SDA/SCL pins!" Are you out of luck? You would be, if you didn't have this ultra-cool TCA9548A 1-to-8 I2C multiplexer! Finally, a way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
